# Fritzing sketch Untitled Sketch (saved by Fritzing 0.9.3b)
breadboards: 1

parts:
  부품1 = GY-VL53L0XV2 Laser Ranger Module
  부품2 = Arduino Leonardo (Rev3b)
  J1 = Basic Servo

nets:
  VCC: 부품1.VCC, 부품2.5V, J1.vcc
  GND: 부품1.GND, 부품2.GND, J1.gnd
  N1: 부품1.SCL, 부품2.SCL
  N2: 부품1.SDA, 부품2.SDA
  N3: 부품2.D5_PWM, J1.pulse

custom parts:
  GY-VL53L0XV2 Laser Ranger Module: The GY-VL53L0XV2 is based on the VL53L0X from ST Microelectronics, a time-of-flight ranging system integrated into a compact module.
