# Fritzing sketch lazer (saved by Fritzing 0.9.3b)

parts:
  부품2 = Arduino Leonardo (Rev3b)
  부품3 = GY-VL53L0XV2 Laser Ranger Module

nets:
  5V: 부품2.5V, 부품3.VCC
  GND: 부품2.GND, 부품3.GND
  N1: 부품2.SDA, 부품3.SDA
  N2: 부품2.SCL, 부품3.SCL

custom parts:
  GY-VL53L0XV2 Laser Ranger Module: The GY-VL53L0XV2 is based on the VL53L0X from ST Microelectronics, a time-of-flight ranging system integrated into a compact module.
